// Logisim project 4BitCPU.circ as structural Verilog: 5 circuits, main circuit main
module main (
  input  [13:0] in_1,
  input  [6:0] in_2
);

  wire and_1_out, clock_1_out, cpu_1_out_en, cpu_1_wr_en, HLT, nor_1_out, RESET_out, Z_FLAG;
  wire [1:0] STATE_REG;
  wire [3:0] cpu_1_acc_out, cpu_1_d, cpu_1_pr_out;
  wire [7:0] cpu_1_addr, cpu_1_d_in, MAR_REG, PC_REG, ram_1_dout;

  Clock clock_1 (.out(clock_1_out));
  Button RESET (.out(RESET_out));
  // LedBar #(.inputtype("row")) ledbar_1: pin names not known; wires that end beside it: MAR_REG
  // LedBar #(.inputtype("row")) ledbar_2: pin names not known; wires that end beside it: PC_REG
  // LedBar #(.inputtype("row"), .matrixcols(2)) ledbar_3: pin names not known; wires that end beside it: STATE_REG
  // LedBar #(.inputtype("row"), .matrixcols(1)) ledbar_4: pin names not known; wires that end beside it: Z_FLAG
  // LedBar #(.inputtype("row"), .matrixcols(1)) ledbar_5: pin names not known; wires that end beside it: HLT
  RAM ram_1 (
    .addr(cpu_1_addr), .we(cpu_1_wr_en), .oe(cpu_1_out_en), .clk(clock_1_out), .din(cpu_1_d_in),
    .dout(ram_1_dout));
  CPU cpu_1 (
    .RST(RESET_out), .D_OUT(ram_1_dout), .CLK(clock_1_out), .D(cpu_1_d), .ACC_OUT(cpu_1_acc_out),
    .PR_OUT(cpu_1_pr_out), .STATE_OUT(STATE_REG), .Z_FLAG_OUT(Z_FLAG), .MAR_OUT(MAR_REG), .D_IN(cpu_1_d_in),
    .ADDR(cpu_1_addr), .WR_EN(cpu_1_wr_en), .OUT_EN(cpu_1_out_en), .PC_OUT(PC_REG), .HLT(HLT));
  Hex_Digit_Display hex_digit_display_1 (.value(cpu_1_acc_out));  // open: dp
  Hex_Digit_Display hex_digit_display_2 (.value(cpu_1_d));  // open: dp
  Hex_Digit_Display hex_digit_display_3 (.value(cpu_1_pr_out));  // open: dp
  nor nor_1 (nor_1_out, cpu_1_acc_out[0], cpu_1_acc_out[1], cpu_1_acc_out[2], cpu_1_acc_out[3]);
  and and_1 (and_1_out, nor_1_out, Z_FLAG);
  // Buzzer buzzer_1: pin names not known; wires that end beside it: in_1, and_1_out, in_2

  // Notes on the sheet:
  //   Accumulator
  //   Data
  //   Page Register
endmodule

module cpu_standalone (
  input  in_1
);

  wire ACC_SEL, alu_1_zero_flag, and_2_out, CLK, clock_1_out, d_ff_1_q, d_ff_1_qn, d_ff_2_q, HLT, IMD,
       LD_ADD, LD_MEM, not_1_out, not_2_out, or_1_out, or_2_out, PC_INC, RST_STATE, UNARY, WR_ACC, WR_IR,
       WR_MEM, WR_PC, WR_PR, WR_ZF, ZERO_FLAG_q;
  wire [1:0] STATE_q;
  wire [2:0] ALU_SEL;
  wire [3:0] ACC_OUT, alu_1_data, IR_q, multiplexer_2_out;
  wire [7:0] MAR, MAR_q, multiplexer_1_out, ram_1_dout;
  wire [7:4] ram_1_dout_2;

  Counter u_MAR (.clr(in_1), .load(LD_ADD), .count(1'b0), .clk(CLK), .D(MAR), .Q(MAR_q));  // open: up, carry
  or or_1 (or_1_out, RST_STATE, PC_INC);
  Multiplexer #(.width(8)) multiplexer_1 (.in0(MAR_q), .in1(ram_1_dout), .out(multiplexer_1_out), .sel(IMD));
  RAM ram_1 (
    .addr(multiplexer_1_out), .we(WR_MEM), .oe(LD_MEM), .clk(CLK), .din({4'b0000, ACC_OUT}),
    .dout({ram_1_dout_2, ram_1_dout[3:0]}));
  Counter PC (.clr(in_1), .load(WR_PC), .clk(or_1_out), .D(ram_1_dout), .Q(MAR));  // open: up, count, carry
  Clock clock_1 (.out(clock_1_out));
  not not_1 (not_1_out, HLT);
  Multiplexer #(.width(4)) multiplexer_2 (
    .in0(ram_1_dout[3:0]), .in1(alu_1_data), .out(multiplexer_2_out), .sel(ACC_SEL));
  // LedBar #(.inputtype("row"), .matrixcols(3)) ledbar_1: pin names not known; wires that end beside it: ALU_SEL
  and and_1 (CLK, not_1_out, clock_1_out);
  Register #(.trigger("falling"), .width(4)) IR (.D(ram_1_dout_2), .en(WR_IR), .clk(CLK), .Q(IR_q), .clr(in_1));
  Register #(.width(4)) ACC (.D(multiplexer_2_out), .en(WR_ACC), .clk(CLK), .Q(ACC_OUT), .clr(in_1));
  Register #(.width(4)) PR (.D(ram_1_dout[3:0]), .en(WR_PR), .clk(CLK), .Q(ram_1_dout[7:4]), .clr(in_1));
  Counter #(.max('h3), .trigger("falling"), .width(2)) STATE (
    .clr(or_2_out), .clk(CLK), .carry(PC_INC), .Q(STATE_q));  // open: load, up, count, D
  D_Flip_Flop d_ff_1 (.D(d_ff_1_qn), .clk(RST_STATE), .Q(d_ff_1_q), .Qn(d_ff_1_qn));  // open: preset, reset
  D_Flip_Flop d_ff_2 (.D(RST_STATE), .clk(CLK), .Q(d_ff_2_q));  // open: Qn, preset, reset
  not not_2 (not_2_out, RST_STATE);
  and and_2 (and_2_out, not_2_out, d_ff_2_q);
  ALU alu_1 (
    .ACC(ACC_OUT), .MDR(ram_1_dout[3:0]), .UNARY(UNARY), .SEL(ALU_SEL), .DATA(alu_1_data),
    .ZERO_FLAG(alu_1_zero_flag));
  or or_2 (or_2_out, and_2_out, in_1);
  Register #(.width(1)) ZERO_FLAG (.D(alu_1_zero_flag), .en(WR_ZF), .clk(CLK), .Q(ZERO_FLAG_q), .clr(in_1));
  CU_LOGIC cu_logic_1 (
    .Z_FLAG(ZERO_FLAG_q), .STATE(STATE_q), .IR(IR_q), .WR_IR(WR_IR), .WR_ACC(WR_ACC), .WR_PR(WR_PR),
    .WR_ZF(WR_ZF), .WR_PC(WR_PC), .IMD(IMD), .ALU_SEL(ALU_SEL), .ACC_SEL(ACC_SEL), .UNARY(UNARY),
    .LD_ADD(LD_ADD), .WR_MEM(WR_MEM), .LD_MEM(LD_MEM), .RST_STATE(RST_STATE), .HLT(HLT));

  // Other names for the same wires on the sheet: RST = in_1
endmodule

module ALU (
  input  [3:0] ACC,
  input  [3:0] MDR,
  input  UNARY,
  input  [2:0] SEL,
  output [3:0] DATA,
  output ZERO_FLAG
);

  wire [3:0] adder_1_out, and_1_out, multiplexer_1_out, or_1_out, subtractor_1_out, xor_1_out;

  Multiplexer #(.width(4)) multiplexer_1 (.in0(MDR), .in1(4'b0001), .out(multiplexer_1_out), .sel(UNARY));
  Adder #(.width(4)) adder_1 (.a(ACC), .b(multiplexer_1_out), .out(adder_1_out));  // open: cin, cout
  Subtractor #(.width(4)) subtractor_1 (.a(ACC), .b(multiplexer_1_out), .out(subtractor_1_out));  // open: bin, bout
  assign and_1_out = ACC & MDR;  // AND_Gate and_1, 4 bits wide
  assign or_1_out = ACC | MDR;  // OR_Gate or_1, 4 bits wide
  assign xor_1_out = ACC ^ MDR;  // XOR_Gate xor_1, 4 bits wide
  Multiplexer #(.select(3), .width(4)) multiplexer_2 (
    .in0(adder_1_out), .in1(subtractor_1_out), .in2(and_1_out), .in3(or_1_out), .in4(xor_1_out), .out(DATA),
    .sel(SEL));  // open: in5, in6, in7
  nor nor_1 (ZERO_FLAG, DATA[0], DATA[1], DATA[2], DATA[3]);
endmodule

module CU_LOGIC (
  input  Z_FLAG,
  input  [1:0] STATE,
  input  [3:0] IR,
  output WR_IR,
  output WR_ACC,
  output WR_PR,
  output WR_ZF,
  output WR_PC,
  output IMD,
  output [2:0] ALU_SEL,
  output ACC_SEL,
  output UNARY,
  output LD_ADD,
  output WR_MEM,
  output LD_MEM,
  output RST_STATE,
  output HLT
);

  wire and_2_out, and_3_out, and_4_out, and_5_out, and_6_out, and_7_out, and_9_out, and_10_out, and_11_out,
       and_12_out, and_13_out, and_14_out, and_15_out, and_16_out, and_17_out, and_18_out, and_19_out,
       and_20_out, and_21_out, and_22_out, and_23_out, and_24_out, and_25_out, and_26_out, and_27_out,
       and_28_out, and_29_out, and_30_out, and_31_out, and_32_out, and_33_out, and_34_out, and_35_out,
       and_36_out, and_37_out, and_38_out, and_39_out, and_40_out, and_41_out, and_42_out, and_43_out,
       and_44_out, and_45_out, and_46_out, and_47_out, and_48_out, and_49_out, and_51_out, and_52_out,
       and_53_out, and_54_out, and_55_out, and_56_out, and_57_out, and_58_out, and_59_out, not_1_out,
       not_2_out, not_3_out, not_4_out, not_5_out, not_6_out, not_7_out;

  not not_1 (not_1_out, Z_FLAG);
  not not_2 (not_2_out, STATE[1]);
  not not_3 (not_3_out, STATE[0]);
  not not_4 (not_4_out, IR[3]);
  not not_5 (not_5_out, IR[2]);
  not not_6 (not_6_out, IR[1]);
  not not_7 (not_7_out, IR[0]);
  and and_1 (WR_IR, not_2_out, not_3_out);
  and and_2 (and_2_out, STATE[1], not_3_out, not_4_out, not_6_out, IR[0]);
  and and_3 (and_3_out, STATE[1], not_3_out, not_4_out, IR[2]);
  and and_4 (and_4_out, STATE[1], not_3_out, IR[3], not_5_out, not_6_out, not_7_out);
  and and_5 (and_5_out, STATE[1], not_3_out, IR[2], not_6_out, IR[0]);
  and and_6 (and_6_out, STATE[1], not_3_out, IR[2], IR[1], not_7_out);
  and and_7 (and_7_out, not_2_out, STATE[0], not_4_out, not_5_out, IR[1], IR[0]);
  and and_8 (WR_PR, not_2_out, STATE[0], IR[3], IR[2], not_6_out, not_7_out);
  and and_9 (and_9_out, STATE[1], not_3_out, not_4_out, IR[2]);
  and and_10 (and_10_out, STATE[1], not_3_out, IR[3], not_5_out, not_6_out, not_7_out);
  and and_11 (and_11_out, STATE[1], not_3_out, IR[2], not_6_out, IR[0]);
  and and_12 (and_12_out, STATE[1], not_3_out, IR[2], IR[1], not_7_out);
  and and_13 (and_13_out, not_2_out, STATE[0], IR[3], not_5_out, not_6_out, IR[0]);
  and and_14 (and_14_out, not_1_out, not_2_out, STATE[0], IR[3], not_5_out, IR[1], not_7_out);
  and and_15 (and_15_out, Z_FLAG, not_2_out, STATE[0], IR[3], not_5_out, IR[0]);
  and and_16 (and_16_out, not_2_out, STATE[0], not_4_out, not_5_out, not_6_out, IR[0]);
  and and_17 (and_17_out, not_2_out, STATE[0], not_4_out, not_5_out, IR[1], not_7_out);
  and and_18 (and_18_out, STATE[1], not_3_out, not_4_out, not_5_out, IR[1], not_7_out);
  and and_19 (and_19_out, not_2_out, STATE[0], IR[3], not_5_out, not_6_out, not_7_out);
  and and_20 (and_20_out, STATE[1], not_3_out, IR[3], not_5_out, not_6_out, not_7_out);
  and and_21 (and_21_out, not_2_out, STATE[0], not_4_out, IR[2], IR[1]);
  and and_22 (and_22_out, STATE[1], not_3_out, not_4_out, IR[2], IR[1]);
  and and_23 (and_23_out, not_2_out, STATE[0], not_4_out, IR[2], IR[0]);
  and and_24 (and_24_out, STATE[1], not_3_out, not_4_out, IR[2], IR[0]);
  and and_25 (and_25_out, not_2_out, STATE[0], IR[3], IR[2], IR[1], not_7_out);
  and and_26 (and_26_out, STATE[1], not_3_out, IR[3], IR[2], IR[1], not_7_out);
  and and_27 (and_27_out, not_2_out, STATE[0], not_4_out, IR[2]);
  and and_28 (and_28_out, not_2_out, STATE[0], IR[3], not_5_out, not_6_out, not_7_out);
  and and_29 (and_29_out, not_2_out, STATE[0], IR[2], not_6_out, IR[0]);
  and and_30 (and_30_out, not_2_out, STATE[0], IR[2], IR[1], not_7_out);
  and and_31 (and_31_out, STATE[1], not_3_out, not_4_out, IR[2]);
  and and_32 (and_32_out, STATE[1], not_3_out, IR[3], not_5_out, not_6_out, not_7_out);
  and and_33 (and_33_out, STATE[1], not_3_out, IR[2], not_6_out, IR[0]);
  and and_34 (and_34_out, STATE[1], not_3_out, IR[2], IR[1], not_7_out);
  and and_35 (and_35_out, not_2_out, STATE[0], IR[3], IR[2], not_6_out, IR[0]);
  and and_36 (and_36_out, STATE[1], not_3_out, IR[3], IR[2], not_6_out, IR[0]);
  and and_37 (and_37_out, not_2_out, STATE[0], IR[3], IR[2], IR[1], not_7_out);
  and and_38 (and_38_out, STATE[1], not_3_out, IR[3], IR[2], IR[1], not_7_out);
  and and_39 (and_39_out, STATE[0], IR[3], not_5_out, IR[0]);
  and and_40 (and_40_out, STATE[0], IR[3], not_5_out, IR[1]);
  and and_41 (and_41_out, STATE[1], not_3_out, not_4_out, not_5_out, IR[1], IR[0]);
  and and_42 (and_42_out, STATE[1], IR[3], not_5_out, not_6_out, IR[0]);
  and and_43 (and_43_out, not_1_out, STATE[1], IR[3], not_5_out, IR[1], not_7_out);
  and and_44 (and_44_out, STATE[1], IR[3], IR[2], not_6_out, not_7_out);
  and and_45 (and_45_out, STATE[1], IR[3], IR[2], IR[1], IR[0]);
  and and_46 (and_46_out, STATE[1], STATE[0], not_6_out);
  and and_47 (and_47_out, STATE[1], STATE[0], not_7_out);
  and and_48 (and_48_out, STATE[1], STATE[0], IR[2]);
  and and_49 (and_49_out, Z_FLAG, STATE[1], IR[3], not_5_out, IR[0]);
  and and_50 (WR_MEM, STATE[1], not_3_out, not_4_out, not_5_out, IR[1], not_7_out);
  and and_51 (and_51_out, not_2_out, not_3_out);
  and and_52 (and_52_out, not_2_out, not_4_out, not_5_out, not_6_out, IR[0]);
  and and_53 (and_53_out, STATE[1], not_3_out, not_4_out, not_5_out, IR[1], IR[0]);
  and and_54 (and_54_out, Z_FLAG, STATE[1], not_3_out, IR[3], not_5_out, IR[1], not_7_out);
  and and_55 (and_55_out, STATE[1], not_3_out, IR[3], IR[2], not_6_out, not_7_out);
  and and_56 (and_56_out, STATE[1], not_3_out, IR[3], IR[2], IR[1], IR[0]);
  and and_57 (and_57_out, not_2_out, STATE[0], IR[3], not_5_out, IR[0]);
  and and_58 (and_58_out, not_2_out, STATE[0], IR[3], not_5_out, IR[1]);
  and and_59 (and_59_out, not_1_out, STATE[1], not_3_out, not_5_out, IR[1], IR[0]);
  and and_60 (HLT, IR[3], IR[2], IR[1], IR[0]);
  or or_1 (WR_ACC, and_2_out, and_3_out, and_4_out, and_5_out, and_6_out, and_7_out);
  or or_2 (WR_ZF, and_9_out, and_10_out, and_11_out, and_12_out);
  or or_3 (WR_PC, and_13_out, and_14_out, and_15_out);
  or or_4 (IMD, and_16_out, and_17_out, and_18_out);
  or or_5 (ALU_SEL[2], and_19_out, and_20_out);
  or or_6 (ALU_SEL[1], and_21_out, and_22_out);
  or or_7 (ALU_SEL[0], and_23_out, and_24_out, and_25_out, and_26_out);
  or or_8 (ACC_SEL, and_27_out, and_28_out, and_29_out, and_30_out, and_31_out, and_32_out, and_33_out, and_34_out);
  or or_9 (UNARY, and_35_out, and_36_out, and_37_out, and_38_out);
  or or_10 (LD_ADD, and_39_out, and_40_out, and_41_out, and_42_out, and_43_out, and_44_out, and_45_out, and_46_out, and_47_out, and_48_out, and_49_out);
  or or_11 (LD_MEM, and_51_out, and_52_out);
  or or_12 (RST_STATE, and_53_out, and_54_out, and_55_out, and_56_out, and_57_out, and_58_out, and_59_out);
endmodule

module CPU (
  input  RST,
  input  CLK,
  input  [7:0] D_OUT,
  output HLT,
  output [1:0] STATE_OUT,
  output [7:0] MAR_OUT,
  output [7:0] ADDR,
  output WR_EN,
  output OUT_EN,
  output [3:0] ACC_OUT,
  output [7:0] D_IN,
  output [3:0] PR_OUT,
  output Z_FLAG_OUT,
  output [3:0] D,
  output [7:0] PC_OUT
);

  wire ACC_SEL, alu_1_zero_flag, and_2_out, CLK_t, d_ff_1_q, IMD, LD_ADD, not_1_out, not_2_out, or_1_out,
       or_2_out, PC_INC, RST_STATE, UNARY, WR_ACC, WR_IR, WR_PC, WR_PR, WR_ZF;
  wire [2:0] ALU_SEL;
  wire [3:0] alu_1_data, IR_q, multiplexer_2_out;

  Counter MAR (.clr(RST), .load(LD_ADD), .count(1'b0), .clk(CLK_t), .D(PC_OUT), .Q(MAR_OUT));  // open: up, carry
  or or_1 (or_1_out, RST_STATE, PC_INC);
  Multiplexer #(.width(8)) multiplexer_1 (.in0(MAR_OUT), .in1({PR_OUT, D_OUT[3:0]}), .out(ADDR), .sel(IMD));
  Counter PC (.clr(RST), .load(WR_PC), .clk(or_1_out), .D({PR_OUT, D_OUT[3:0]}), .Q(PC_OUT));  // open: up, count, carry
  not not_1 (not_1_out, HLT);
  Multiplexer #(.width(4)) multiplexer_2 (.in0(D_OUT[3:0]), .in1(alu_1_data), .out(multiplexer_2_out), .sel(ACC_SEL));
  // LedBar #(.inputtype("row"), .matrixcols(3)) ledbar_1: pin names not known; wires that end beside it: ALU_SEL
  and and_1 (CLK_t, not_1_out, CLK);
  Register #(.trigger("falling"), .width(4)) IR (.D(D_OUT[7:4]), .en(WR_IR), .clk(CLK_t), .Q(IR_q), .clr(RST));
  Register #(.width(4)) ACC (.D(multiplexer_2_out), .en(WR_ACC), .clk(CLK_t), .Q(ACC_OUT), .clr(RST));
  Register #(.width(4)) PR (.D(D_OUT[3:0]), .en(WR_PR), .clk(CLK_t), .Q(PR_OUT), .clr(RST));
  Counter #(.max('h3), .trigger("falling"), .width(2)) STATE (
    .clr(or_2_out), .clk(CLK_t), .carry(PC_INC), .Q(STATE_OUT));  // open: load, up, count, D
  D_Flip_Flop d_ff_1 (.D(RST_STATE), .clk(CLK_t), .Q(d_ff_1_q));  // open: Qn, preset, reset
  not not_2 (not_2_out, RST_STATE);
  and and_2 (and_2_out, not_2_out, d_ff_1_q);
  ALU alu_1 (
    .ACC(ACC_OUT), .MDR(D_OUT[3:0]), .UNARY(UNARY), .SEL(ALU_SEL), .DATA(alu_1_data),
    .ZERO_FLAG(alu_1_zero_flag));
  or or_2 (or_2_out, and_2_out, RST);
  Register #(.width(1)) ZERO_FLAG (.D(alu_1_zero_flag), .en(WR_ZF), .clk(CLK_t), .Q(Z_FLAG_OUT), .clr(RST));
  CU_LOGIC cu_logic_1 (
    .Z_FLAG(Z_FLAG_OUT), .STATE(STATE_OUT), .IR(IR_q), .WR_IR(WR_IR), .WR_ACC(WR_ACC), .WR_PR(WR_PR),
    .WR_ZF(WR_ZF), .WR_PC(WR_PC), .IMD(IMD), .ALU_SEL(ALU_SEL), .ACC_SEL(ACC_SEL), .UNARY(UNARY),
    .LD_ADD(LD_ADD), .WR_MEM(WR_EN), .LD_MEM(OUT_EN), .RST_STATE(RST_STATE), .HLT(HLT));

  assign D = D_OUT[3:0];
  assign D_IN = {4'b0000, ACC_OUT};

  // Other names for the same wires on the sheet: LD_MEM = OUT_EN; MAR[7:0] = PC_OUT; WR_MEM = WR_EN
endmodule
